// Logisim project ALU.circ as structural Verilog: 1 circuit, main circuit main
// ALU
module main (
  input  [31:0] ALU_SOURCE_X,
  input  [31:0] ALU_SOURCE_Y,
  input  [3:0] ALU_OPERATION,
  output LT,
  output EQ,
  output GT,
  output [31:0] ALU_RESULT,
  output ADD_OVERFLOW,
  output SUB_OVERFLOW,
  output DIV_BY_ZERO
);

  wire adder_2_cout, adder_3_cout, adder_4_cout, adder_5_cout, adder_6_cout, adder_7_cout, adder_8_cout,
       or_2_out;
  wire [4:0] bit_extender_1_out, bit_extender_2_out;
  wire [31:0] adder_1_out, adder_2_out, adder_3_out, adder_4_out, adder_5_out, adder_6_out, adder_7_out,
       adder_8_out, and_1_out, divider_2_out, multiplier_1_out, not_1_out, or_1_out, shifter_1_out,
       shifter_2_out, shifter_3_out, shifter_4_out, subtractor_1_out, undriven, xor_1_out;

  Divider #(.width(32)) divider_1 (.a(ALU_SOURCE_Y), .upper(undriven));  // open: b, out, rem
  Shifter #(.width(32), .shift("lr")) shifter_1 (.in(ALU_SOURCE_X), .\dist (5'b10000), .out(shifter_1_out));
  Shifter #(.width(32)) shifter_2 (.in(shifter_1_out), .\dist (5'b10000), .out(shifter_2_out));
  Bit_Extender #(.in_width(32), .out_width(5)) bit_extender_1 (.in(ALU_SOURCE_Y), .out(bit_extender_1_out));
  Bit_Extender #(.in_width(32), .out_width(5)) bit_extender_2 (.in(ALU_SOURCE_Y), .out(bit_extender_2_out));
  Adder #(.width(32)) adder_1 (.a(shifter_2_out), .b(undriven), .out(adder_1_out));  // open: cin, cout
  Shifter #(.width(32)) shifter_3 (.in(ALU_SOURCE_X), .\dist (bit_extender_1_out), .out(shifter_3_out));
  Shifter #(.width(32), .shift("lr")) shifter_4 (.in(ALU_SOURCE_X), .\dist (bit_extender_2_out), .out(shifter_4_out));
  assign and_1_out = ALU_SOURCE_X & ALU_SOURCE_Y;  // AND_Gate and_1, 32 bits wide
  assign or_1_out = ALU_SOURCE_X | ALU_SOURCE_Y;  // OR_Gate or_1, 32 bits wide
  assign xor_1_out = ALU_SOURCE_X ^ ALU_SOURCE_Y;  // XOR_Gate xor_1, 32 bits wide
  Divider #(.width(32)) divider_2 (.a(ALU_SOURCE_X), .b(ALU_SOURCE_Y), .out(divider_2_out));  // open: upper, rem
  Multiplier #(.width(32)) multiplier_1 (
    .a(ALU_SOURCE_X), .b(ALU_SOURCE_Y), .out(multiplier_1_out));  // open: cin, cout
  Subtractor #(.width(32)) subtractor_1 (
    .a(ALU_SOURCE_X), .b(ALU_SOURCE_Y), .out(subtractor_1_out), .bout(SUB_OVERFLOW));  // open: bin
  Adder #(.width(32)) adder_2 (
    .a(ALU_SOURCE_X), .b(ALU_SOURCE_Y), .out(adder_2_out), .cout(adder_2_cout));  // open: cin
  Adder #(.width(32)) adder_3 (
    .a(ALU_SOURCE_X), .b(ALU_SOURCE_Y), .out(adder_3_out), .cout(adder_3_cout));  // open: cin
  Adder #(.width(32)) adder_4 (
    .a(ALU_SOURCE_X), .b(ALU_SOURCE_Y), .out(adder_4_out), .cout(adder_4_cout));  // open: cin
  Adder #(.width(32)) adder_5 (
    .a(ALU_SOURCE_X), .b(ALU_SOURCE_Y), .out(adder_5_out), .cout(adder_5_cout));  // open: cin
  Adder #(.width(32)) adder_6 (
    .a(ALU_SOURCE_X), .b(ALU_SOURCE_Y), .out(adder_6_out), .cout(adder_6_cout));  // open: cin
  Adder #(.width(32)) adder_7 (
    .a(ALU_SOURCE_X), .b(ALU_SOURCE_Y), .out(adder_7_out), .cout(adder_7_cout));  // open: cin
  Adder #(.width(32)) adder_8 (
    .a(ALU_SOURCE_X), .b(ALU_SOURCE_Y), .out(adder_8_out), .cout(adder_8_cout));  // open: cin
  Multiplexer #(.select(4), .width(32)) multiplexer_1 (
    .in0(shifter_3_out), .in1(shifter_4_out), .in2(and_1_out), .in3(or_1_out), .in4(xor_1_out),
    .in5(divider_2_out), .in6(multiplier_1_out), .in7(adder_1_out), .in8(subtractor_1_out),
    .in9(adder_2_out), .in10(adder_3_out), .in11(adder_4_out), .in12(adder_5_out), .in13(adder_6_out),
    .in14(adder_7_out), .in15(adder_8_out), .out(ALU_RESULT), .sel(ALU_OPERATION));  // open: en
  Comparator #(.width(32), .mode("unsigned")) comparator_1 (
    .a(ALU_SOURCE_X), .b(ALU_SOURCE_Y), .gt(GT), .eq(EQ), .lt(LT));
  assign not_1_out = ~ALU_SOURCE_Y;  // NOT_Gate not_1, 32 bits wide
  or or_2 (or_2_out, adder_6_cout, adder_7_cout, adder_8_cout);
  Bit_Extender #(.in_width(32), .out_width(1)) bit_extender_3 (.in(not_1_out), .out(DIV_BY_ZERO));
  or or_3 (ADD_OVERFLOW, adder_3_cout, adder_2_cout, adder_4_cout, adder_5_cout, or_2_out);

  // Other names for the same wires on the sheet: s1[31:0] = ALU_SOURCE_X; s2[31:0] = ALU_SOURCE_Y

  // Notes on the sheet:
  //   ALU MODULE
endmodule
