// Logisim project CMP.circ as structural Verilog: 1 circuit, main circuit main
// CMP
module main (
  input  LT,
  input  EQ,
  input  GT,
  input  [2:0] CQ_QUERY,
  input  CR_WRITE,
  input  CLOCK,
  output [2:0] CR_VAL,
  output CQ_PASSED
);

  wire comparator_1_eq, comparator_2_eq, comparator_3_eq, not_1_out, or_2_out, or_3_out;

  Register #(.width(3)) CQ_Register (.D(CQ_QUERY), .en(CR_WRITE), .Q(CR_VAL), .clk(CLOCK));  // open: clr
  Comparator #(.width(1), .mode("unsigned")) comparator_1 (
    .a(GT), .b(CR_VAL[0]), .eq(comparator_1_eq));  // open: gt, lt
  Comparator #(.width(1), .mode("unsigned")) comparator_2 (
    .a(CR_VAL[1]), .b(EQ), .eq(comparator_2_eq));  // open: gt, lt
  Comparator #(.width(1), .mode("unsigned")) comparator_3 (
    .a(CR_VAL[2]), .b(LT), .eq(comparator_3_eq));  // open: gt, lt
  or or_1 (CQ_PASSED, comparator_1_eq, comparator_2_eq, comparator_3_eq);
  or or_2 (or_2_out, EQ, GT);
  not not_1 (not_1_out, EQ);
  or or_3 (or_3_out, EQ, LT);
  Multiplexer #(.select(2)) multiplexer_1 (.in0(LT), .in2(EQ), .in3(GT));  // open: in1, out, sel, en
  Multiplexer #(.select(3), .enable("false")) multiplexer_2 (
    .in0(1'b0), .in1(GT), .in2(EQ), .in3(or_2_out), .in4(LT), .in5(not_1_out), .in6(or_3_out), .in7(1'b1),
    .sel(CQ_QUERY));  // open: out

  // Other names for the same wires on the sheet: clk = CLOCK; cqPass = CQ_PASSED; crWrite = CR_WRITE; tunnel = LT;
  //   tunnel_t = EQ; tunnel_t_t = GT

  // Notes on the sheet:
  //   CR MODULE
endmodule
