// Logisim project CPU.circ as structural Verilog: 1 circuit, main circuit main
// CPU
module main (
  input  [31:0] INSTRUCTION,
  input  [23:0] CURRENT_PC,
  input  CQ_PASSED,
  input  [31:0] REG_1_VAL,
  input  [31:0] REG_2_VAL,
  input  [31:0] REG_3_VAL,
  input  [31:0] ALU_RESULT,
  input  [31:0] MEM_OUT,
  output [23:0] JUMP_ADDRESS,
  output [2:0] CQ_QUERY,
  output CR_WRITE,
  output [3:0] REG_1_READ,
  output [3:0] REG_2_READ,
  output [3:0] REG_3_WRITE,
  output [31:0] REG_WRITE_VAL,
  output REG_WRITE,
  output [31:0] ALU_SOURCE_X,
  output [31:0] ALU_SOURCE_Y,
  output [3:0] ALU_OPERATION,
  output [23:0] MEM_ADDR,
  output [31:0] MEM_IN,
  output SHL,
  output SHR,
  output AND,
  output IOR,
  output XOR,
  output STU,
  output MUL,
  output DIV,
  output SUB,
  output ADD,
  output MLD,
  output MST,
  output STL,
  output LNK,
  output JMP,
  output MEM_WRITE
);

  wire ALUctr_0_out, ALUctr_1_out, ALUSrc_out, clk, comparator_1_eq, comparator_2_eq, comparator_3_eq,
       comparator_5_eq, comparator_6_lt, CQ_Cmd, CQ_Output, Jump_Cmd, Link_Cmd, Load_Cmd, MemtoReg, memWrite,
       multiplexer_6_out, not_2_out, not_3_out, not_4_out, not_5_out, nPC_sel, or_1_out, prev_jump,
       RegDst_out, RegWrite_out, write;
  wire [0:0] ExtOp_out;
  wire [1:0] A_Type, undriven_3;
  wire [3:0] undriven, undriven_2;
  wire [31:0] bit_extender_1_out, bit_extender_2_out, bit_extender_3_out, REG_1_VAL_t, REG_2_VAL_t, RI_OUT;

  Multiplexer #(.width(4), .enable("false")) multiplexer_1 (
    .in0(INSTRUCTION[3:0]), .in1(undriven), .out(REG_1_READ), .sel(INSTRUCTION[24]));
  assign bit_extender_1_out = {{16{1'b0}}, {INSTRUCTION[15:4], undriven_2}};  // Bit_Extender bit_extender_1
  assign bit_extender_2_out = {{12{1'b0}}, INSTRUCTION[19:0]};  // Bit_Extender bit_extender_2
  assign bit_extender_3_out = {{8{1'b0}}, INSTRUCTION[23:0]};  // Bit_Extender bit_extender_3
  Multiplexer #(.width(32), .enable("false")) multiplexer_2 (
    .in0(MEM_OUT), .out(REG_WRITE_VAL), .sel(MemtoReg));  // open: in1
  Multiplexer #(.width(4), .enable("false")) multiplexer_3 (
    .in0(INSTRUCTION[19:16]), .in1(INSTRUCTION[3:0]), .out(REG_1_READ), .sel(ALUSrc_out));
  Multiplexer #(.select(2), .width(32), .enable("false")) multiplexer_4 (
    .in0(REG_1_VAL_t), .in1(REG_2_VAL_t), .in2(REG_3_VAL), .sel(undriven_3));  // open: in3, out
  Multiplexer #(.width(4), .enable("false")) multiplexer_5 (
    .in0(INSTRUCTION[3:0]), .in1(INSTRUCTION[19:16]), .out(REG_2_READ), .sel(ALUSrc_out));
  Demultiplexer #(.width(32)) demultiplexer_1 (
    .out0(REG_WRITE_VAL), .in(ALU_RESULT), .sel(RegDst_out));  // open: out1, en
  Multiplexer #(.enable("false")) multiplexer_6 (.out(multiplexer_6_out), .sel(REG_WRITE));  // open: in0, in1
  Demultiplexer #(.select(2), .width(32)) demultiplexer_2 (
    .out0(bit_extender_1_out), .out1(bit_extender_2_out), .out2(bit_extender_3_out), .in(RI_OUT),
    .sel({JMP, ExtOp_out[0]}));  // open: out3, en
  Comparator #(.width(4), .mode("unsigned")) comparator_1 (
    .a(INSTRUCTION[31:28]), .b(4'b1111), .eq(comparator_1_eq));  // open: gt, lt
  Comparator #(.width(4), .mode("unsigned")) comparator_2 (
    .a(INSTRUCTION[31:28]), .b(4'b1010), .eq(comparator_2_eq));  // open: gt, lt
  Comparator #(.width(4), .mode("unsigned")) comparator_3 (
    .a(INSTRUCTION[31:28]), .b(4'b1011), .eq(comparator_3_eq));  // open: gt, lt
  Multiplexer #(.width(4), .enable("false")) multiplexer_7 ();  // open: in0, in1, out, sel
  or ALUSrc (ALUSrc_out, STU, SUB, STL, LNK);
  not not_1 (REG_WRITE, RegWrite_out);
  or RegWrite (RegWrite_out, MST, CR_WRITE, JMP);
  or ExtOp (ExtOp_out[0], STL, CR_WRITE, LNK, JMP);
  // OR_Gate ALUctr_0 has open pins: out=ALUctr_0_out
  // OR_Gate ALUctr_1 has open pins: out=ALUctr_1_out
  and and_1 (Jump_Cmd, comparator_1_eq, prev_jump, CQ_Output);
  and and_2 (Load_Cmd, comparator_2_eq, prev_jump, CQ_Output);
  and and_3 (memWrite, comparator_3_eq, prev_jump, CQ_Output);
  not not_2 (not_2_out, INSTRUCTION[28]);
  not not_3 (not_3_out, INSTRUCTION[29]);
  not not_4 (not_4_out, INSTRUCTION[30]);
  not not_5 (not_5_out, INSTRUCTION[31]);
  or RegDst (RegDst_out, MST, CR_WRITE);
  buf u_MemWrite (MEM_WRITE, MST);  // OR_Gate
  buf u_MemtoReg (MemtoReg, MLD);  // OR_Gate
  buf u_nPC_sel (nPC_sel, JMP);  // OR_Gate
  and u_SHL (SHL, not_2_out, not_3_out, not_4_out, not_5_out);
  and AND_4 (AND, not_2_out, INSTRUCTION[28], not_4_out, not_5_out);
  and u_SHR (SHR, INSTRUCTION[28], not_3_out, not_4_out, not_5_out);
  and u_IOR (IOR, INSTRUCTION[28], INSTRUCTION[29], not_4_out, not_5_out);
  Comparator #(.width(4), .mode("unsigned")) comparator_4 (
    .a(INSTRUCTION[31:28]), .b(4'b1110), .eq(Link_Cmd));  // open: gt, lt
  and u_XOR (XOR, not_2_out, not_3_out, INSTRUCTION[30], not_5_out);
  Comparator #(.width(2)) comparator_5 (.a(2'b01), .b(A_Type), .eq(comparator_5_eq));  // open: gt, lt
  Comparator #(.width(4), .mode("unsigned")) comparator_6 (
    .a(INSTRUCTION[31:28]), .b(4'b1011), .lt(comparator_6_lt));  // open: gt, eq
  and u_STU (STU, INSTRUCTION[28], not_4_out, INSTRUCTION[30], not_5_out);
  and and_5 (CQ_Cmd, comparator_5_eq, prev_jump, CQ_Output);
  or or_1 (or_1_out, comparator_6_lt, Link_Cmd);
  and u_MUL (MUL, not_2_out, INSTRUCTION[29], INSTRUCTION[30], not_5_out);
  and and_6 (write, CQ_Output, prev_jump, clk, or_1_out);
  and u_DIV (DIV, INSTRUCTION[28], INSTRUCTION[29], INSTRUCTION[30], not_5_out);
  and u_SUB (SUB, not_2_out, not_3_out, not_4_out, INSTRUCTION[31]);
  and u_MLD (MLD, not_2_out, INSTRUCTION[29], not_4_out, INSTRUCTION[31]);
  and u_ADD (ADD, INSTRUCTION[28], not_3_out, not_4_out, INSTRUCTION[31]);
  and u_MST (MST, INSTRUCTION[28], not_3_out, not_4_out, INSTRUCTION[31]);
  and u_STL (STL, not_2_out, not_4_out, INSTRUCTION[30], INSTRUCTION[31]);
  and CMP (CR_WRITE, INSTRUCTION[28], not_3_out, INSTRUCTION[30], INSTRUCTION[31]);
  and u_LNK (LNK, not_2_out, INSTRUCTION[29], INSTRUCTION[30], INSTRUCTION[31]);
  and u_JMP (JMP, INSTRUCTION[28], INSTRUCTION[29], INSTRUCTION[30], INSTRUCTION[31]);

  assign ALU_OPERATION = INSTRUCTION[31:28];
  assign ALU_SOURCE_X = REG_1_VAL;
  assign ALU_SOURCE_Y = REG_2_VAL;
  assign CQ_QUERY = INSTRUCTION[27:25];

  // Other names for the same wires on the sheet: CMP = CR_WRITE; RI[3:0] = INSTRUCTION[3:0];
  //   IMM[11:0] = INSTRUCTION[15:4]; RS[3:0] = INSTRUCTION[19:16]; RD[3:0] = INSTRUCTION[23:20];
  //   IS_RI = INSTRUCTION[24]; _CQ[2:0] = INSTRUCTION[27:25]; OP_Code[3:0] = INSTRUCTION[31:28];
  //   MEM_ID[31:0] = MEM_IN; memStore = MEM_WRITE; Save_Cmd = memWrite

  // Notes on the sheet:
  //   INSTRUCTION MODULE
  //   CR MODULE
  //   REGISTER FILE MODULE
  //   ALU MODULE
  //   MEMORY MODULE
  //   This Could Be Wrong
  //   Control
  //   Can REG write?
  //   Is this  set CQ command?
endmodule
