// Logisim project NPC.circ as structural Verilog: 1 circuit, main circuit main
// NPC
module main (
  input  CQ_PASSED,
  input  in_2,
  input  [31:0] INSTRUCTION,
  input  [23:0] CURRENT_PC,
  input  [23:0] JUMP_ADDRESS,
  input  jump,
  output [23:0] NEXT_PC
);

  wire clk, jcontrol, Jump_Cmd, prev_jump, register_1_q;
  wire [3:0] bit_extender_1_out;
  wire [4:0] undriven;
  wire [23:0] bit_extender_2_out, bit_extender_3_out, multiplexer_1_out, multiplexer_2_out, undriven_3;
  wire [31:0] shifter_1_out, shifter_2_out, undriven_2;

  not not_1 (prev_jump, register_1_q);
  Register #(.width(1)) register_1 (.D(Jump_Cmd), .Q(register_1_q), .clk(clk));  // open: en, clr
  Multiplexer #(.width(24), .enable("false")) multiplexer_1 (
    .in0(CURRENT_PC), .in1(JUMP_ADDRESS), .out(multiplexer_1_out), .sel(jcontrol));
  Multiplexer #(.width(24)) multiplexer_2 (
    .in0({24{1'b0}}), .in1(multiplexer_1_out), .out(multiplexer_2_out), .sel(CQ_PASSED));  // open: en
  Shifter #(.width(32), .shift("lr")) shifter_1 (.in(INSTRUCTION), .\dist (5'b11100), .out(shifter_1_out));
  Bit_Extender #(.in_width(32), .out_width(4)) bit_extender_1 (.in(shifter_1_out), .out(bit_extender_1_out));
  Comparator #(.width(4)) comparator_1 (.a(4'b1111), .b(bit_extender_1_out), .eq(jcontrol));  // open: gt, lt
  assign bit_extender_2_out = {{23{1'b0}}, 1'b1};  // Bit_Extender bit_extender_2
  Adder #(.width(24)) adder_1 (.a(bit_extender_2_out), .b(multiplexer_2_out), .out(NEXT_PC));  // open: cin, cout
  // NOT_Gate not_2 has open pins: in=Jump_Cmd, out=open
  Register #(.width(32)) Instruction_Register (.D(INSTRUCTION), .en(CQ_PASSED), .clk(in_2));  // open: Q, clr
  Comparator #(.width(32)) comparator_2 (.a(undriven_2), .b(shifter_2_out));  // open: gt, eq, lt
  Shifter #(.width(32), .shift("lr")) shifter_2 (.\dist (undriven), .out(shifter_2_out));  // open: in
  Bit_Extender #(.in_width(1), .out_width(24)) bit_extender_3 (.out(bit_extender_3_out));  // open: in
  Register #(.width(24)) pc (.D(undriven_3), .en(CQ_PASSED), .clk(in_2));  // open: Q, clr

  // Other names for the same wires on the sheet: clock = in_2; cPC[23:0] = CURRENT_PC; cqpass = CQ_PASSED;
  //   inst[31:0] = INSTRUCTION; j[23:0] = JUMP_ADDRESS; nextPC[23:0] = NEXT_PC

  // Notes on the sheet:
  //   NPC MODULE
endmodule
