// Logisim project PIP.circ as structural Verilog: 1 circuit, main circuit main
// PIP
module main (
  input  CQ_PASSED,
  input  [31:0] INSTRUCTION_IN,
  input  [23:0] PC_IN,
  input  CLOCK,
  output [31:0] INSTRUCTION_OUT,
  output [23:0] PC_OUT
);

  wire and_1_out, and_2_out, jcontrol, not_1_out, not_2_out;
  wire [3:0] bit_extender_1_out;
  wire [23:0] multiplexer_2_out, pc_reg_2_q, pc_reg_q, undriven, undriven_2;
  wire [31:0] inst_reg_q, multiplexer_1_out, shifter_1_out;

  Register #(.width(24)) pc_reg (.D(undriven_2), .en(CQ_PASSED), .Q(pc_reg_q), .clk(CLOCK));  // open: clr
  and and_1 (and_1_out, CQ_PASSED, not_1_out);
  not not_1 (not_1_out, jcontrol);
  Multiplexer #(.width(32)) multiplexer_1 (
    .in0({32{1'b0}}), .in1(INSTRUCTION_IN), .out(multiplexer_1_out), .sel(and_1_out));  // open: en
  Register #(.width(32)) inst_reg (.D(multiplexer_1_out), .en(CQ_PASSED), .Q(inst_reg_q), .clk(CLOCK));  // open: clr
  and and_2 (and_2_out, CQ_PASSED, not_2_out);
  not not_2 (not_2_out, jcontrol);
  Multiplexer #(.width(24)) multiplexer_2 (
    .in0({24{1'b0}}), .in1(undriven), .out(multiplexer_2_out), .sel(and_2_out));  // open: en
  Register #(.width(24)) pc_reg_2 (.D(multiplexer_2_out), .en(CQ_PASSED), .Q(pc_reg_2_q), .clk(CLOCK));  // open: clr
  Shifter #(.width(32), .shift("lr")) shifter_1 (.in(INSTRUCTION_IN), .\dist (5'b11100), .out(shifter_1_out));
  Bit_Extender #(.in_width(32), .out_width(4)) bit_extender_1 (.in(shifter_1_out), .out(bit_extender_1_out));
  Comparator #(.width(4)) comparator_1 (.a(4'b1111), .b(bit_extender_1_out), .eq(jcontrol));  // open: gt, lt

  assign INSTRUCTION_OUT = INSTRUCTION_IN;
  assign PC_OUT = PC_IN;

  // Other names for the same wires on the sheet: clk = CLOCK; cqpass = CQ_PASSED; in[31:0] = INSTRUCTION_IN;
  //   inst[31:0] = INSTRUCTION_IN

  // Notes on the sheet:
  //   PIPELINE MODULE
endmodule
