// Logisim project REG.circ as structural Verilog: 1 circuit, main circuit Ida Register File
// Register File
module Ida_Register_File (
  input  [3:0] Read_Reg_1,
  input  [3:0] Read_Reg_2,
  input  [3:0] Write_Reg,
  input  [23:0] Write_Value,
  input  Reg_Write,
  input  Clock,
  output [23:0] Reg_1_Value,
  output [23:0] Reg_2_Value,
  output [23:0] Reg_3_Value,
  output [23:0] r00,
  output [23:0] r01,
  output [23:0] r02,
  output [23:0] r03,
  output [23:0] r04,
  output [23:0] r05,
  output [23:0] r06,
  output [23:0] r07,
  output [23:0] r08,
  output [23:0] r09,
  output [23:0] r10,
  output [23:0] r11,
  output [23:0] r12,
  output [23:0] r13,
  output [23:0] r14,
  output [23:0] r15
);

  wire and_1_out, clk00, clk01, clk02, clk03, clk04, clk05, clk06, clk07, clk08, clk09, clk10, clk11, clk12,
       clk13, clk14, clk15;
  wire [23:0] wR00, wR01, wR02, wR03, wR04, wR05, wR06, wR07, wR08, wR09, wR10, wR11, wR12, wR13, wR14, wR15;

  // Probe on Read_Reg_1
  // Probe on Read_Reg_2
  // Probe on Write_Reg
  // Probe on Write_Value
  // Probe on Reg_Write
  // Probe on Clock
  // Probe on Reg_1_Value
  // Probe on Reg_2_Value
  // Probe on Reg_3_Value
  // Probe on r00
  // Probe on r01
  // Probe on r02
  // Probe on r03
  // Probe on r04
  // Probe on r05
  // Probe on r06
  // Probe on r07
  // Probe on r08
  // Probe on r09
  // Probe on r10
  // Probe on r11
  // Probe on r12
  // Probe on r13
  // Probe on r14
  // Probe on r15
  and and_1 (and_1_out, Clock, Reg_Write);
  Demultiplexer #(.select(4), .width(24)) demultiplexer_1 (
    .out0(wR00), .out1(wR01), .out2(wR02), .out3(wR03), .out4(wR04), .out5(wR05), .out6(wR06), .out7(wR07),
    .out8(wR08), .out9(wR09), .out10(wR10), .out11(wR11), .out12(wR12), .out13(wR13), .out14(wR14),
    .out15(wR15), .in(Write_Value), .sel(Write_Reg));  // open: en
  Demultiplexer #(.select(4)) demultiplexer_2 (
    .out0(clk00), .out1(clk01), .out2(clk02), .out3(clk03), .out4(clk04), .out5(clk05), .out6(clk06),
    .out7(clk07), .out8(clk08), .out9(clk09), .out10(clk10), .out11(clk11), .out12(clk12), .out13(clk13),
    .out14(clk14), .out15(clk15), .in(and_1_out), .sel(Write_Reg));  // open: en
  Register #(.width(24)) u_R00 (.D(wR00), .Q(r00), .clk(clk00));  // open: en, clr
  Register #(.width(24)) u_R01 (.D(wR01), .Q(r01), .clk(clk01));  // open: en, clr
  Register #(.width(24)) u_R02 (.D(wR02), .Q(r02), .clk(clk02));  // open: en, clr
  Register #(.width(24)) u_R03 (.D(wR03), .Q(r03), .clk(clk03));  // open: en, clr
  Register #(.width(24)) u_R04 (.D(wR04), .Q(r04), .clk(clk04));  // open: en, clr
  Register #(.width(24)) u_R05 (.D(wR05), .Q(r05), .clk(clk05));  // open: en, clr
  Register #(.width(24)) u_R06 (.D(wR06), .Q(r06), .clk(clk06));  // open: en, clr
  Register #(.width(24)) u_R07 (.D(wR07), .Q(r07), .clk(clk07));  // open: en, clr
  Register #(.width(24)) u_R08 (.D(wR08), .Q(r08), .clk(clk08));  // open: en, clr
  Register #(.width(24)) u_R09 (.D(wR09), .Q(r09), .clk(clk09));  // open: en, clr
  Register #(.width(24)) u_R10 (.D(wR10), .Q(r10), .clk(clk10));  // open: en, clr
  Register #(.width(24)) u_R11 (.D(wR11), .Q(r11), .clk(clk11));  // open: en, clr
  Register #(.width(24)) u_R12 (.D(wR12), .Q(r12), .clk(clk12));  // open: en, clr
  Register #(.width(24)) u_R13 (.D(wR13), .Q(r13), .clk(clk13));  // open: en, clr
  Register #(.width(24)) u_R14 (.D(wR14), .Q(r14), .clk(clk14));  // open: en, clr
  Register #(.width(24)) u_R15 (.D(wR15), .Q(r15), .clk(clk15));  // open: en, clr
  Multiplexer #(.select(4), .width(24)) multiplexer_1 (
    .in0(r00), .in1(r01), .in2(r02), .in3(r03), .in4(r04), .in5(r05), .in6(r06), .in7(r07), .in8(r08),
    .in9(r09), .in10(r10), .in11(r11), .in12(r12), .in13(r13), .in14(r14), .in15(r15), .out(Reg_1_Value),
    .sel(Read_Reg_1));  // open: en
  Multiplexer #(.select(4), .width(24)) multiplexer_2 (
    .in0(r00), .in1(r01), .in2(r02), .in3(r03), .in4(r04), .in5(r05), .in6(r06), .in7(r07), .in8(r08),
    .in9(r09), .in10(r10), .in11(r11), .in12(r12), .in13(r13), .in14(r14), .in15(r15), .out(Reg_2_Value),
    .sel(Read_Reg_2));  // open: en
  Multiplexer #(.select(4), .width(24)) multiplexer_3 (
    .in0(r00), .in1(r01), .in2(r02), .in3(r03), .in4(r04), .in5(r05), .in6(r06), .in7(r07), .in8(r08),
    .in9(r09), .in10(r10), .in11(r11), .in12(r12), .in13(r13), .in14(r14), .in15(r15), .out(Reg_3_Value),
    .sel(Write_Reg));  // open: en

  // Other names for the same wires on the sheet: clk = Clock; IR00[23:0] = r00; IR01[23:0] = r01; IR02[23:0] = r02;
  //   IR03[23:0] = r03; IR04[23:0] = r04; IR05[23:0] = r05; IR06[23:0] = r06; IR07[23:0] = r07; IR08[23:0] = r08;
  //   IR09[23:0] = r09; IR10[23:0] = r10; IR11[23:0] = r11; IR12[23:0] = r12; IR13[23:0] = r13; IR14[23:0] = r14;
  //   IR15[23:0] = r15; reg1Read[3:0] = Read_Reg_1; reg1Val[23:0] = Reg_1_Value; reg2Read[3:0] = Read_Reg_2;
  //   reg2Val[23:0] = Reg_2_Value; reg3Val[23:0] = Reg_3_Value; reg3Write[3:0] = Write_Reg; write = Reg_Write;
  //   writeVal[23:0] = Write_Value

  // Notes on the sheet:
  //   INPUT PINS
  //   INPUT PROBES
  //   OUTPUT PROBES
  //   OUTPUT PINS
  //   DO NOT MOVE/ADD/CHANGE ANY INPUT OR OUTPUT PINS!
endmodule
