// Logisim project ALU eh.circ as structural Verilog: 1 circuit, main circuit Ida ALU
// ALU
module Ida_ALU (
  input  [23:0] ALU_Source_1,
  input  [23:0] ALU_Source_2,
  input  [3:0] Operation,
  output [23:0] ALU_Result
);

  wire [2:0] comparator_1_gt, comparator_2_gt;
  wire [4:0] bit_extender_1_out, bit_extender_2_out, bit_extender_3_out, bit_extender_4_out,
       bit_extender_5_out;
  wire [23:0] adder_1_out, adder_2_out, adder_3_out, and_1_out, bit_extender_6_out, bit_extender_7_out,
       or_1_out, shifter_1_out, shifter_2_out, shifter_3_out, shifter_4_out, shifter_5_out, subtractor_1_out,
       xor_1_out;

  // Probe on ALU_Source_1
  // Probe on ALU_Source_2
  // Probe on Operation
  // Probe on ALU_Result
  Bit_Extender #(.in_width(24), .out_width(5)) bit_extender_1 (.in(ALU_Source_2), .out(bit_extender_1_out));
  Bit_Extender #(.in_width(24), .out_width(5)) bit_extender_2 (.in(ALU_Source_2), .out(bit_extender_2_out));
  Bit_Extender #(.in_width(24), .out_width(5)) bit_extender_3 (.in(ALU_Source_2), .out(bit_extender_3_out));
  Bit_Extender #(.in_width(24), .out_width(5)) bit_extender_4 (.in(ALU_Source_2), .out(bit_extender_4_out));
  Bit_Extender #(.in_width(24), .out_width(5)) bit_extender_5 (.in(ALU_Source_2), .out(bit_extender_5_out));
  Shifter #(.width(24)) shifter_1 (.in(ALU_Source_1), .\dist (bit_extender_1_out), .out(shifter_1_out));
  Shifter #(.width(24), .shift("lr")) shifter_2 (.in(ALU_Source_1), .\dist (bit_extender_2_out), .out(shifter_2_out));
  Shifter #(.width(24), .shift("ar")) shifter_3 (.in(ALU_Source_1), .\dist (bit_extender_3_out), .out(shifter_3_out));
  Shifter #(.width(24), .shift("rl")) shifter_4 (.in(ALU_Source_1), .\dist (bit_extender_4_out), .out(shifter_4_out));
  Shifter #(.width(24), .shift("rr")) shifter_5 (.in(ALU_Source_1), .\dist (bit_extender_5_out), .out(shifter_5_out));
  Adder #(.width(24)) adder_1 (.a(ALU_Source_1), .b(ALU_Source_2), .out(adder_1_out));  // open: cin, cout
  Subtractor #(.width(24)) subtractor_1 (
    .a(ALU_Source_1), .b(ALU_Source_2), .out(subtractor_1_out));  // open: bin, bout
  Adder #(.width(24)) adder_2 (.a(ALU_Source_1), .b(ALU_Source_2), .out(adder_2_out));  // open: cin, cout
  Adder #(.width(24)) adder_3 (.a(ALU_Source_1), .b(ALU_Source_2), .out(adder_3_out));  // open: cin, cout
  Comparator #(.width(24)) comparator_1 (
    .a(ALU_Source_1), .b(ALU_Source_2), .gt(comparator_1_gt[0]), .eq(comparator_1_gt[1]),
    .lt(comparator_1_gt[2]));
  Comparator #(.width(24), .mode("unsigned")) comparator_2 (
    .a(ALU_Source_1), .b(ALU_Source_2), .gt(comparator_2_gt[0]), .eq(comparator_2_gt[1]),
    .lt(comparator_2_gt[2]));
  assign and_1_out = ALU_Source_1 & ALU_Source_2;  // AND_Gate and_1, 24 bits wide
  assign or_1_out = ALU_Source_1 | ALU_Source_2;  // OR_Gate or_1, 24 bits wide
  assign xor_1_out = ALU_Source_1 ^ ALU_Source_2;  // XOR_Gate xor_1, 24 bits wide
  assign bit_extender_6_out = {{21{1'b0}}, comparator_1_gt};  // Bit_Extender bit_extender_6
  assign bit_extender_7_out = {{21{1'b0}}, comparator_2_gt};  // Bit_Extender bit_extender_7
  Multiplexer #(.select(4), .width(24)) multiplexer_1 (
    .in0(shifter_1_out), .in1(shifter_2_out), .in2(shifter_3_out), .in3(shifter_4_out), .in4(shifter_5_out),
    .in5(and_1_out), .in6(or_1_out), .in7(xor_1_out), .in8(adder_1_out), .in9(subtractor_1_out),
    .in10(adder_2_out), .in11(adder_3_out), .in12(bit_extender_6_out), .in13(bit_extender_7_out),
    .out(ALU_Result), .sel(Operation));  // open: in14, in15, en

  // Other names for the same wires on the sheet: op[3:0] = Operation; result[23:0] = ALU_Result;
  //   s1[23:0] = ALU_Source_1; s2[23:0] = ALU_Source_2

  // Notes on the sheet:
  //   INPUTS
  //   INPUT PROBES
  //   DO NOT MOVE/ADD/CHANGE ANY INPUT OR OUTPUT PINS!
  //   OUTPUT PROBES
  //   OUTPUT
endmodule
