// Logisim project ALU.circ as structural Verilog: 1 circuit, main circuit Ida ALU
// ALU
module Ida_ALU (
  input  [23:0] ALU_Source_1,
  input  [23:0] ALU_Source_2,
  input  [3:0] Operation,
  output [23:0] ALU_Result
);

  // Probe on ALU_Source_1
  // Probe on ALU_Source_2
  // Probe on Operation
  // Probe on ALU_Result

  // Other names for the same wires on the sheet: op[3:0] = Operation; result[23:0] = ALU_Result;
  //   s1[23:0] = ALU_Source_1; s2[23:0] = ALU_Source_2

  // Notes on the sheet:
  //   INPUTS
  //   INPUT PROBES
  //   DO NOT MOVE/ADD/CHANGE ANY INPUT OR OUTPUT PINS!
  //   OUTPUT PROBES
  //   OUTPUT
endmodule
