// Logisim project CPU 11.circ as structural Verilog: 1 circuit, main circuit Ida CPU
// CPU
module Ida_CPU (
  input  [31:0] Instruction,
  input  Clock,
  output [23:0] Mem_Data,
  output [23:0] Mem_Address,
  output Mem_Write,
  output [23:0] Next_PC,
  output [23:0] r00,
  output [23:0] r01,
  output [23:0] r02,
  output [23:0] r03,
  output [23:0] r04,
  output [23:0] r05,
  output [23:0] r06,
  output [23:0] r07,
  output [23:0] r08,
  output [23:0] r09,
  output [23:0] r10,
  output [23:0] r11,
  output [23:0] r12,
  output [23:0] r13,
  output [23:0] r14,
  output [23:0] r15,
  output [3:0] out_23,
  output [23:0] out_24,
  output [23:0] out_25,
  output [23:0] out_26,
  output [3:0] out_27,
  output [23:0] out_28,
  output [23:0] out_29,
  output [23:0] out_30
);

  wire and_4_out, and_5_out, comparator_1_lt, comparator_2_gt, comparator_3_eq, comparator_4_eq,
       comparator_5_eq, comparator_8_eq, comparator_9_eq, controlled_buffer_4_out, CQ_Cmd, CQ_Output,
       Jump_Cmd, Link_Cmd, Load_Cmd, not_1_out, not_2_out, not_3_out, or_1_out, or_2_out, or_3_out, or_4_out,
       tunnel, tunnel_t, tunnel_t_t, will_write_to_reg, write;
  wire [1:0] A_Type;
  wire [3:0] multiplexer_2_out;
  wire [23:0] adder_1_out, bit_extender_1_out, bit_extender_2_out, bit_extender_3_out, Immediate_Value,
       multiplexer_7_out, ram_1_data, RD_Result, RI_Result, RS_Result;
  wire [23:3] CQ_Register_q;

  // Probe on Instruction
  // Probe on Clock
  // Probe on r00
  // Probe on r01
  // Probe on r02
  // Probe on r03
  // Probe on r04
  // Probe on r05
  // Probe on r06
  // Probe on r07
  // Probe on Mem_Data
  // Probe on Mem_Address
  // Probe on Mem_Write
  // Probe on Next_PC
  // Probe on r08
  // Probe on r09
  // Probe on r10
  // Probe on r11
  // Probe on r12
  // Probe on r13
  // Probe on r14
  // Probe on r15
  Comparator #(.width(4), .mode("unsigned")) comparator_1 (
    .a(Instruction[31:28]), .b(4'b1100), .lt(comparator_1_lt));  // open: gt, eq
  Comparator #(.width(4), .mode("unsigned")) comparator_2 (
    .a(Instruction[31:28]), .b(4'b1101), .gt(comparator_2_gt));  // open: eq, lt
  not not_1 (not_1_out, or_1_out);
  or or_1 (or_1_out, comparator_1_lt, comparator_2_gt);
  assign A_Type = comparator_1_lt ? 2'b10 : 2'bz;  // Controlled_Buffer controlled_buffer_1
  assign A_Type = not_1_out ? 2'b01 : 2'bz;  // Controlled_Buffer controlled_buffer_2
  assign A_Type = comparator_2_gt ? 2'b00 : 2'bz;  // Controlled_Buffer controlled_buffer_3
  Comparator #(.width(4), .mode("unsigned")) comparator_3 (
    .a(Instruction[31:28]), .b(4'b1111), .eq(comparator_3_eq));  // open: gt, lt
  and and_1 (Jump_Cmd, comparator_3_eq, CQ_Output);
  Comparator #(.width(4), .mode("unsigned")) comparator_4 (
    .a(Instruction[31:28]), .b(4'b1010), .eq(comparator_4_eq));  // open: gt, lt
  and and_2 (Load_Cmd, comparator_4_eq, CQ_Output);
  Comparator #(.width(4), .mode("unsigned")) comparator_5 (
    .a(Instruction[31:28]), .b(4'b1011), .eq(comparator_5_eq));  // open: gt, lt
  and and_3 (Mem_Write, comparator_5_eq, CQ_Output);
  assign bit_extender_1_out = {{4{1'b0}}, Instruction[19:0]};  // Bit_Extender bit_extender_1
  assign bit_extender_2_out = {{8{1'b0}}, Instruction[15:0]};  // Bit_Extender bit_extender_2
  Multiplexer #(.select(2), .width(24), .enable("false")) multiplexer_1 (
    .in0(Instruction[23:0]), .in1(bit_extender_1_out), .in2(bit_extender_2_out), .out(out_26), .sel(A_Type));  // open: in3
  Comparator #(.width(4), .mode("unsigned")) comparator_6 (
    .a(Instruction[31:28]), .b(4'b1011), .lt(will_write_to_reg));  // open: gt, eq
  Comparator #(.width(4), .mode("unsigned")) comparator_7 (
    .a(Instruction[31:28]), .b(4'b1110), .eq(Link_Cmd));  // open: gt, lt
  Comparator #(.width(2)) comparator_8 (.a(2'b01), .b(A_Type), .eq(comparator_8_eq));  // open: gt, lt
  and and_4 (and_4_out, Clock, will_write_to_reg);
  and and_5 (and_5_out, Clock, Link_Cmd);
  and and_6 (CQ_Cmd, comparator_8_eq, CQ_Output);
  and and_7 (write, CQ_Output, and_4_out);
  and and_8 (write, CQ_Output, and_5_out);
  Multiplexer #(.width(4), .enable("false")) multiplexer_2 (
    .in0(Instruction[23:20]), .in1(4'b0010), .out(multiplexer_2_out), .sel(Link_Cmd));
  Ida_Register_File ida_register_file_1 (
    .Read_Reg_1(Instruction[3:0]), .Read_Reg_2(Instruction[19:16]), .Write_Reg(multiplexer_2_out),
    .Write_Value(out_30), .Reg_1_Value(RI_Result), .Reg_2_Value(RS_Result), .Reg_Write(write), .Clock(Clock),
    .r00(r00), .r01(r01), .r02(r02), .r03(r03), .r04(r04), .r05(r05), .r06(r06), .r07(r07), .r08(r08),
    .r09(r09), .r10(r10), .r11(r11), .r12(r12), .r13(r13), .r14(r14), .r15(r15), .Reg_3_Value(RD_Result));
  assign controlled_buffer_4_out = CQ_Cmd ? Clock : 1'bz;  // Controlled_Buffer controlled_buffer_4
  Register #(.width(24)) CQ_Register (
    .D(out_25), .Q({CQ_Register_q, tunnel_t_t, tunnel_t, tunnel}), .clk(controlled_buffer_4_out));  // open: en, clr
  Multiplexer #(.width(24), .enable("false")) multiplexer_3 (
    .in0(RI_Result), .in1(out_26), .out(Immediate_Value), .sel(Instruction[24]));
  Multiplexer #(.width(24), .enable("false")) multiplexer_4 (
    .in0(RS_Result), .in1(RD_Result), .out(out_24), .sel(comparator_9_eq));
  Comparator #(.width(2)) comparator_9 (.a(A_Type), .b(2'b01), .eq(comparator_9_eq));  // open: gt, lt
  or or_2 (or_2_out, tunnel_t, tunnel);
  or or_3 (or_3_out, tunnel_t, tunnel_t_t);
  not not_2 (not_2_out, tunnel_t);
  Multiplexer #(.select(3), .enable("false")) multiplexer_5 (
    .in0(1'b0), .in1(or_2_out), .in2(tunnel_t_t), .in3(not_2_out), .in4(tunnel_t), .in5(or_3_out),
    .in6(tunnel), .in7(1'b1), .out(CQ_Output), .sel(Instruction[27:25]));
  Ida_ALU ida_alu_1 (.ALU_Source_1(out_24), .ALU_Source_2(out_28), .Operation(Instruction[31:28]), .ALU_Result(out_25));
  RAM #(.addrWidth(24), .dataWidth(24), .bus("separate")) ram_1 (
    .addr(out_25), .din(RD_Result), .data(ram_1_data), .str(Mem_Write), .ld(Load_Cmd));  // open: sel, clk, clr
  Multiplexer #(.width(24), .enable("false")) multiplexer_6 (
    .in0(out_25), .in1(Immediate_Value), .out(out_30), .sel(Link_Cmd));
  assign out_30 = Load_Cmd ? ram_1_data : 24'bz;  // Controlled_Buffer controlled_buffer_5
  assign bit_extender_3_out = {{23{1'b0}}, 1'b1};  // Bit_Extender bit_extender_3
  Adder #(.width(24)) adder_1 (.a(bit_extender_3_out), .b(Next_PC), .out(adder_1_out));  // open: cin, cout
  not not_3 (not_3_out, Jump_Cmd);
  Multiplexer #(.width(24), .enable("false")) multiplexer_7 (
    .in0(out_28), .in1(adder_1_out), .out(multiplexer_7_out), .sel(not_3_out));
  assign Mem_Address = or_4_out ? out_25 : 24'bz;  // Controlled_Buffer controlled_buffer_6
  or or_4 (or_4_out, Mem_Write, Load_Cmd);
  assign Mem_Data = Mem_Write ? RD_Result : 24'bz;  // Controlled_Buffer controlled_buffer_7
  Register #(.width(24)) pc (.D(multiplexer_7_out), .Q(Next_PC), .clk(Clock));  // open: en, clr

  assign out_23 = Instruction[31:28];
  assign out_27 = Instruction[31:28];
  assign out_29 = out_25;

  // Other names for the same wires on the sheet: ALU_Input_1[23:0] = out_24; ALU_Input_2[23:0] = out_28;
  //   ALU_Result[23:0] = out_25; clk = Clock; Direct_Immediate_Value[23:0] = out_26; inst[31:0] = Instruction;
  //   RI_Select[3:0] = Instruction[3:0]; RS_Select[3:0] = Instruction[19:16]; RD_Select[3:0] = Instruction[23:20];
  //   Immediate = Instruction[24]; CQ[2:0] = Instruction[27:25]; OP_Code[3:0] = Instruction[31:28];
  //   memAddr[23:0] = Mem_Address; memData[23:0] = Mem_Data; memWrite = Mem_Write; Save_Cmd = Mem_Write;
  //   nextPC[23:0] = Next_PC; Write_Val[23:0] = out_30

  // Notes on the sheet:
  //   INPUTS
  //   INPUT PROBES
  //   OUTPUT PROBES
  //   OUTPUTS
  //   DO NOT MOVE/ADD/CHANGE ANY INPUT OR OUTPUT PINS!
  //   A-Type Selector
  //   Input Interpretation
  //   Control
  //   CM Stuff
  //   Gather Inputs
  //   Create Value
  //   Result
endmodule
