// Logisim project CPU 16.circ as structural Verilog: 1 circuit, main circuit Ida CPU
// CPU
module Ida_CPU (
  input  [31:0] Instruction,
  input  Clock,
  output [23:0] Mem_Data,
  output [23:0] Mem_Address,
  output Mem_Write,
  output [23:0] Next_PC,
  output [23:0] r00,
  output [23:0] r01,
  output [23:0] r02,
  output [23:0] r03,
  output [23:0] r04,
  output [23:0] r05,
  output [23:0] r06,
  output [23:0] r07,
  output [23:0] r08,
  output [23:0] r09,
  output [23:0] r10,
  output [23:0] r11,
  output [23:0] r12,
  output [23:0] r13,
  output [23:0] r14,
  output [23:0] r15,
  output [2:0] out_23,
  output [23:0] out_24,
  output [23:0] out_25,
  output [3:0] out_26,
  output [23:0] out_27,
  output [23:0] out_28,
  output [23:0] out_29,
  output [3:0] out_30,
  output [23:0] out_31
);

  wire comparator_1_eq, comparator_2_eq, comparator_3_eq, comparator_4_lt, comparator_5_gt, comparator_7_eq,
       comparator_8_lt, comparator_9_eq, controlled_buffer_4_out, CQ_Cmd, CQ_Output, Jump_Cmd, Link_Cmd,
       Load_Cmd, not_1_out, not_2_out, not_3_out, not_4_out, or_1_out, or_2_out, or_3_out, or_4_out,
       or_5_out, register_1_q, tunnel, tunnel_t, tunnel_t_t, write;
  wire [1:0] A_Type;
  wire [3:0] multiplexer_3_out;
  wire [23:0] adder_1_out, bit_extender_1_out, bit_extender_2_out, bit_extender_3_out, multiplexer_7_out,
       multiplexer_9_out, ram_1_data, RD_Result, RI_Result, RS_Result;
  wire [23:3] CQ_Register_q;
  wire [24:0] current_inst;
  wire [31:0] multiplexer_1_out;

  // Probe on Instruction
  // Probe on Clock
  // Probe on r00
  // Probe on r01
  // Probe on r02
  // Probe on r03
  // Probe on r04
  // Probe on r05
  // Probe on r06
  // Probe on r07
  // Probe on Mem_Data
  // Probe on Mem_Address
  // Probe on Mem_Write
  // Probe on Next_PC
  // Probe on r08
  // Probe on r09
  // Probe on r10
  // Probe on r11
  // Probe on r12
  // Probe on r13
  // Probe on r14
  // Probe on r15
  Register #(.width(32)) Instruction_Register (
    .D(multiplexer_1_out), .Q({out_26, out_23, current_inst}), .clk(not_1_out));  // open: en, clr
  Multiplexer #(.width(32), .enable("false")) multiplexer_1 (
    .in0(Instruction), .in1(32'h8f000000), .out(multiplexer_1_out), .sel(Jump_Cmd));
  not not_1 (not_1_out, Clock);
  Register #(.width(1)) register_1 (.D(Jump_Cmd), .Q(register_1_q), .clk(Clock));  // open: en, clr
  Comparator #(.width(4), .mode("unsigned")) comparator_1 (
    .a(out_26), .b(4'b1111), .eq(comparator_1_eq));  // open: gt, lt
  and and_1 (Jump_Cmd, comparator_1_eq, CQ_Output);
  Comparator #(.width(4), .mode("unsigned")) comparator_2 (
    .a(out_26), .b(4'b1010), .eq(comparator_2_eq));  // open: gt, lt
  and and_2 (Load_Cmd, comparator_2_eq, CQ_Output);
  Comparator #(.width(4), .mode("unsigned")) comparator_3 (
    .a(out_26), .b(4'b1011), .eq(comparator_3_eq));  // open: gt, lt
  and and_3 (Mem_Write, comparator_3_eq, CQ_Output);
  Comparator #(.width(4), .mode("unsigned")) comparator_4 (
    .a(out_26), .b(4'b1100), .lt(comparator_4_lt));  // open: gt, eq
  Comparator #(.width(4), .mode("unsigned")) comparator_5 (
    .a(out_26), .b(4'b1101), .gt(comparator_5_gt));  // open: eq, lt
  or or_1 (or_1_out, comparator_4_lt, comparator_5_gt);
  not not_2 (not_2_out, or_1_out);
  assign bit_extender_1_out = {{4{1'b0}}, current_inst[19:0]};  // Bit_Extender bit_extender_1
  assign bit_extender_2_out = {{8{1'b0}}, current_inst[15:0]};  // Bit_Extender bit_extender_2
  assign A_Type = comparator_4_lt ? 2'b10 : 2'bz;  // Controlled_Buffer controlled_buffer_1
  assign A_Type = not_2_out ? 2'b01 : 2'bz;  // Controlled_Buffer controlled_buffer_2
  assign A_Type = comparator_5_gt ? 2'b00 : 2'bz;  // Controlled_Buffer controlled_buffer_3
  Multiplexer #(.select(2), .width(24), .enable("false")) multiplexer_2 (
    .in0(current_inst[23:0]), .in1(bit_extender_1_out), .in2(bit_extender_2_out), .out(out_31), .sel(A_Type));  // open: in3
  Comparator #(.width(4), .mode("unsigned")) comparator_6 (.a(out_26), .b(4'b1110), .eq(Link_Cmd));  // open: gt, lt
  Comparator #(.width(2)) comparator_7 (.a(2'b01), .b(A_Type), .eq(comparator_7_eq));  // open: gt, lt
  Comparator #(.width(4), .mode("unsigned")) comparator_8 (
    .a(out_26), .b(4'b1011), .lt(comparator_8_lt));  // open: gt, eq
  and and_4 (CQ_Cmd, comparator_7_eq, CQ_Output);
  or or_2 (or_2_out, comparator_8_lt, Link_Cmd);
  and and_5 (write, CQ_Output, Clock, or_2_out);
  Multiplexer #(.width(4), .enable("false")) multiplexer_3 (
    .in0(current_inst[23:20]), .in1(4'b0010), .out(multiplexer_3_out), .sel(Link_Cmd));
  Ida_Register_File ida_register_file_1 (
    .Read_Reg_1(current_inst[3:0]), .Read_Reg_2(current_inst[19:16]), .Write_Reg(multiplexer_3_out),
    .Write_Value(out_29), .Reg_1_Value(RI_Result), .Reg_2_Value(RS_Result), .Reg_Write(write), .Clock(Clock),
    .r00(r00), .r01(r01), .r02(r02), .r03(r03), .r04(r04), .r05(r05), .r06(r06), .r07(r07), .r08(r08),
    .r09(r09), .r10(r10), .r11(r11), .r12(r12), .r13(r13), .r14(r14), .r15(r15), .Reg_3_Value(RD_Result));
  assign controlled_buffer_4_out = CQ_Cmd ? Clock : 1'bz;  // Controlled_Buffer controlled_buffer_4
  Register #(.width(24)) CQ_Register (
    .D(out_25), .Q({CQ_Register_q, tunnel_t_t, tunnel_t, tunnel}), .clk(controlled_buffer_4_out));  // open: en, clr
  Multiplexer #(.width(24), .enable("false")) multiplexer_4 (
    .in0(RI_Result), .in1(out_31), .out(out_27), .sel(current_inst[24]));
  Multiplexer #(.width(24), .enable("false")) multiplexer_5 (
    .in0(RS_Result), .in1(RD_Result), .out(out_24), .sel(comparator_9_eq));
  Comparator #(.width(2)) comparator_9 (.a(A_Type), .b(2'b01), .eq(comparator_9_eq));  // open: gt, lt
  or or_3 (or_3_out, tunnel_t, tunnel);
  or or_4 (or_4_out, tunnel_t, tunnel_t_t);
  not not_3 (not_3_out, tunnel_t);
  Multiplexer #(.select(3), .enable("false")) multiplexer_6 (
    .in0(1'b0), .in1(or_3_out), .in2(tunnel_t_t), .in3(not_3_out), .in4(tunnel_t), .in5(or_4_out),
    .in6(tunnel), .in7(1'b1), .out(CQ_Output), .sel(out_23));
  Ida_ALU ida_alu_1 (.ALU_Source_1(out_24), .ALU_Source_2(out_27), .Operation(out_26), .ALU_Result(out_25));
  RAM #(.addrWidth(24), .dataWidth(24), .bus("separate")) ram_1 (
    .addr(out_25), .din(RD_Result), .data(ram_1_data), .str(Mem_Write), .ld(Load_Cmd));  // open: sel, clk, clr
  Multiplexer #(.width(24), .enable("false")) multiplexer_7 (
    .in0(out_25), .in1(out_27), .out(multiplexer_7_out), .sel(Link_Cmd));
  Multiplexer #(.width(24), .enable("false")) multiplexer_8 (
    .in0(multiplexer_7_out), .in1(ram_1_data), .out(out_29), .sel(Load_Cmd));
  assign bit_extender_3_out = {{23{1'b0}}, 1'b1};  // Bit_Extender bit_extender_3
  Adder #(.width(24)) adder_1 (.a(bit_extender_3_out), .b(Next_PC), .out(adder_1_out));  // open: cin, cout
  not not_4 (not_4_out, Jump_Cmd);
  Multiplexer #(.width(24), .enable("false")) multiplexer_9 (
    .in0(out_27), .in1(adder_1_out), .out(multiplexer_9_out), .sel(not_4_out));
  assign Mem_Address = or_5_out ? out_25 : 24'bz;  // Controlled_Buffer controlled_buffer_5
  or or_5 (or_5_out, Mem_Write, Load_Cmd);
  assign Mem_Data = Mem_Write ? RD_Result : 24'bz;  // Controlled_Buffer controlled_buffer_6
  Register #(.width(24)) pc (.D(multiplexer_9_out), .Q(Next_PC), .clk(Clock));  // open: en, clr

  assign out_28 = out_25;
  assign out_30 = out_26;

  // Other names for the same wires on the sheet: ALU_Input_1[23:0] = out_24; ALU_Result[23:0] = out_25; clk = Clock;
  //   RI_Select[3:0] = current_inst[3:0]; RS_Select[3:0] = current_inst[19:16]; RD_Select[3:0] = current_inst[23:20];
  //   Immediate = current_inst[24]; CQ[2:0] = out_23; current_inst[31:25] = {out_26, out_23}; OP_Code[3:0] = out_26;
  //   Direct_Immediate_Value[23:0] = out_31; Immediate_Value[23:0] = out_27; inst[31:0] = Instruction;
  //   memAddr[23:0] = Mem_Address; memData[23:0] = Mem_Data; memWrite = Mem_Write; Save_Cmd = Mem_Write;
  //   nextPC[23:0] = Next_PC; Write_Val[23:0] = out_29

  // Notes on the sheet:
  //   INPUTS
  //   INPUT PROBES
  //   OUTPUT PROBES
  //   OUTPUTS
  //   DO NOT MOVE/ADD/CHANGE ANY INPUT OR OUTPUT PINS!
  //   Input Interpretation
  //   Control
  //   A-Type Selector
  //   Is this  set CQ command?
  //   Can REG write?
  //   CM Stuff
  //   Gather Inputs
  //   Create Value
  //   Result
endmodule
