// Logisim project CPU 3.circ as structural Verilog: 1 circuit, main circuit Ida CPU
// CPU
module Ida_CPU (
  input  [31:0] Instruction,
  input  Clock,
  input  in_3,
  output [23:0] Mem_Data,
  output [23:0] Mem_Address,
  output Mem_Write,
  output [23:0] Next_PC,
  output [23:0] r00,
  output [23:0] r01,
  output [23:0] r02,
  output [23:0] r03,
  output [23:0] r04,
  output [23:0] r05,
  output [23:0] r06,
  output [23:0] r07,
  output [23:0] r08,
  output [23:0] r09,
  output [23:0] r10,
  output [23:0] r11,
  output [23:0] r12,
  output [23:0] r13,
  output [23:0] r14,
  output [23:0] r15
);

  wire comparator_1_lt, comparator_2_gt, comparator_6_lt, comparator_7_eq, comparator_8_eq,
       controlled_buffer_5_out, CQ_Output, Jump_Command, Load_Command, not_1_out, not_2_out, or_1_out,
       or_2_out, or_3_out, Save_Command, tunnel, tunnel_t, tunnel_t_t, will_write_to_reg;
  wire [1:0] A_Type;
  wire [20:0] CQ_Register_q;
  wire [23:0] adder_1_out, ALU_Input_1, ALU_Input_2, ALU_Result, bit_extender_1_out, bit_extender_2_out,
       bit_extender_3_out, Direct_Immediate_Value, multiplexer_5_out, RD_Result, RI_Result, RS_Result,
       Write_Val;

  // Probe on Instruction
  // Probe on Clock
  // Probe on r00
  // Probe on r01
  // Probe on r02
  // Probe on r03
  // Probe on r04
  // Probe on r05
  // Probe on r06
  // Probe on r07
  // Probe on Mem_Data
  // Probe on Mem_Address
  // Probe on Mem_Write
  // Probe on Next_PC
  // Probe on r08
  // Probe on r09
  // Probe on r10
  // Probe on r11
  // Probe on r12
  // Probe on r13
  // Probe on r14
  // Probe on r15
  Comparator #(.width(4), .mode("unsigned")) comparator_1 (
    .a(Instruction[31:28]), .b(4'b1100), .lt(comparator_1_lt));  // open: gt, eq
  Comparator #(.width(4), .mode("unsigned")) comparator_2 (
    .a(Instruction[31:28]), .b(4'b1101), .gt(comparator_2_gt));  // open: eq, lt
  or or_1 (or_1_out, comparator_1_lt, comparator_2_gt);
  not not_1 (not_1_out, or_1_out);
  assign A_Type = comparator_1_lt ? 2'b10 : 2'bz;  // Controlled_Buffer controlled_buffer_1
  assign A_Type = not_1_out ? 2'b01 : 2'bz;  // Controlled_Buffer controlled_buffer_2
  assign A_Type = comparator_2_gt ? 2'b00 : 2'bz;  // Controlled_Buffer controlled_buffer_3
  Comparator #(.width(4), .mode("unsigned")) comparator_3 (
    .a(Instruction[31:28]), .b(4'b1111), .eq(Jump_Command));  // open: gt, lt
  Comparator #(.width(4), .mode("unsigned")) comparator_4 (
    .a(Instruction[31:28]), .b(4'b1010), .eq(Load_Command));  // open: gt, lt
  Comparator #(.width(4), .mode("unsigned")) comparator_5 (
    .a(Instruction[31:28]), .b(4'b1011), .eq(Save_Command));  // open: gt, lt
  assign bit_extender_1_out = {{8{1'b0}}, Instruction[15:0]};  // Bit_Extender bit_extender_1
  assign bit_extender_2_out = {{4{1'b0}}, Instruction[19:0]};  // Bit_Extender bit_extender_2
  Multiplexer #(.select(2), .width(24), .enable("false")) multiplexer_1 (
    .in0(bit_extender_1_out), .in1(bit_extender_2_out), .in2(Instruction[23:0]),
    .out(Direct_Immediate_Value), .sel(A_Type));  // open: in3
  assign will_write_to_reg = comparator_6_lt ? Clock : 1'bz;  // Controlled_Buffer controlled_buffer_4
  Comparator #(.width(4), .mode("unsigned")) comparator_6 (
    .a(Instruction[31:28]), .b(4'b1011), .lt(comparator_6_lt));  // open: gt, eq
  assign controlled_buffer_5_out = comparator_7_eq ? Clock : 1'bz;  // Controlled_Buffer controlled_buffer_5
  Comparator #(.width(2)) comparator_7 (.a(2'b01), .b(A_Type), .eq(comparator_7_eq));  // open: gt, lt
  Register #(.width(24)) CQ_Register (
    .D(ALU_Result), .Q({tunnel, tunnel_t, tunnel_t_t, CQ_Register_q}), .clk(controlled_buffer_5_out));  // open: en, clr
  Ida_Register_File ida_register_file_1 (
    .Read_Reg_1(Instruction[3:0]), .Read_Reg_2(Instruction[19:16]), .Write_Reg(Instruction[23:20]),
    .Write_Value(Write_Val), .Reg_1_Value(RI_Result), .Reg_2_Value(RS_Result), .Reg_Write(in_3),
    .Clock(Clock), .r00(r00), .r01(r01), .r02(r02), .r03(r03), .r04(r04), .r05(r05), .r06(r06), .r07(r07),
    .r08(r08), .r09(r09), .r10(r10), .r11(r11), .r12(r12), .r13(r13), .r14(r14), .r15(r15),
    .Reg_3_Value(RD_Result));
  RAM #(.addrWidth(24), .dataWidth(24), .bus("separate")) ram_1 (
    .addr(ALU_Result), .din(RD_Result), .data(Write_Val), .str(Save_Command), .ld(Load_Command));  // open: sel, clk, clr
  or or_2 (or_2_out, tunnel_t, tunnel);
  not not_2 (not_2_out, tunnel_t);
  or or_3 (or_3_out, tunnel_t, tunnel_t_t);
  Multiplexer #(.select(3), .enable("false")) multiplexer_2 (
    .in0(1'b0), .in1(or_2_out), .in2(tunnel_t_t), .in3(not_2_out), .in4(tunnel_t), .in5(or_3_out),
    .in6(tunnel), .in7(1'b1), .out(CQ_Output), .sel(Instruction[27:25]));
  Comparator #(.width(2)) comparator_8 (.a(A_Type), .b(2'b01), .eq(comparator_8_eq));  // open: gt, lt
  Multiplexer #(.width(24), .enable("false")) multiplexer_3 (
    .in0(RI_Result), .in1(Direct_Immediate_Value), .out(ALU_Input_2), .sel(Instruction[24]));
  Multiplexer #(.width(24), .enable("false")) multiplexer_4 (
    .in0(RS_Result), .in1(RD_Result), .out(ALU_Input_1), .sel(comparator_8_eq));
  assign bit_extender_3_out = {{23{1'b0}}, 1'b1};  // Bit_Extender bit_extender_3
  Adder #(.width(24)) adder_1 (.a(bit_extender_3_out), .b(Next_PC), .out(adder_1_out));  // open: cin, cout
  Ida_ALU ida_alu_1 (
    .ALU_Source_1(ALU_Input_1), .ALU_Source_2(ALU_Input_2), .Operation(Instruction[31:28]),
    .ALU_Result(ALU_Result));
  assign Write_Val = will_write_to_reg ? ALU_Result : 24'bz;  // Controlled_Buffer controlled_buffer_6
  Multiplexer #(.width(24), .enable("false")) multiplexer_5 (
    .in0(RI_Result), .in1(adder_1_out), .out(multiplexer_5_out), .sel(Jump_Command));
  Register #(.width(24)) pc (.D(multiplexer_5_out), .Q(Next_PC), .clk(Clock));  // open: en, clr

  // Other names for the same wires on the sheet: clk = Clock; inst[31:0] = Instruction;
  //   RI_Select[3:0] = Instruction[3:0]; RS_Select[3:0] = Instruction[19:16]; RD_Select[3:0] = Instruction[23:20];
  //   Immediate = Instruction[24]; CQ[2:0] = Instruction[27:25]; OP_Code[3:0] = Instruction[31:28];
  //   memAddr[23:0] = Mem_Address; memData[23:0] = Mem_Data; memWrite = Mem_Write; nextPC[23:0] = Next_PC;
  //   write = in_3

  // Notes on the sheet:
  //   INPUTS
  //   INPUT PROBES
  //   OUTPUT PROBES
  //   OUTPUTS
  //   DO NOT MOVE/ADD/CHANGE ANY INPUT OR OUTPUT PINS!
  //   A-Type Selector
  //   Control
  //   Input Interpretation
  //   CM Stuff
  //   Gather Inputs
  //   Create Value
  //   Result
endmodule
