// Logisim project CPU 8.circ as structural Verilog: 1 circuit, main circuit Ida CPU
// CPU
module Ida_CPU (
  input  [31:0] Instruction,
  input  Clock,
  output [23:0] Mem_Data,
  output [23:0] Mem_Address,
  output Mem_Write,
  output [23:0] Next_PC,
  output [23:0] r00,
  output [23:0] r01,
  output [23:0] r02,
  output [23:0] r03,
  output [23:0] r04,
  output [23:0] r05,
  output [23:0] r06,
  output [23:0] r07,
  output [23:0] r08,
  output [23:0] r09,
  output [23:0] r10,
  output [23:0] r11,
  output [23:0] r12,
  output [23:0] r13,
  output [23:0] r14,
  output [23:0] r15,
  output [3:0] out_23,
  output [23:0] out_24,
  output [23:0] out_25,
  output [23:0] out_26,
  output [23:0] out_27,
  output [23:0] out_28,
  output [3:0] out_29,
  output [23:0] out_30,
  output [23:0] out_31,
  output [23:0] out_32,
  output [23:0] out_33,
  output [23:0] out_34,
  output [23:0] out_35
);

  wire comparator_1_lt, comparator_2_gt, comparator_3_eq, comparator_4_eq, comparator_5_eq, comparator_7_eq,
       comparator_8_eq, controlled_buffer_4_out, controlled_buffer_5_out, CQ_Cmd, CQ_Output, Jump_Cmd,
       Load_Cmd, not_1_out, not_2_out, or_1_out, or_2_out, or_3_out, or_4_out, tunnel, tunnel_t, tunnel_t_t,
       will_write_to_reg, write;
  wire [1:0] A_Type;
  wire [23:0] adder_1_out, bit_extender_1_out, bit_extender_2_out, bit_extender_3_out, multiplexer_5_out,
       RD_Result, RS_Result;
  wire [23:3] CQ_Register_q;

  // Probe on Instruction
  // Probe on Clock
  // Probe on r00
  // Probe on r01
  // Probe on r02
  // Probe on r03
  // Probe on r04
  // Probe on r05
  // Probe on r06
  // Probe on r07
  // Probe on Mem_Data
  // Probe on Mem_Address
  // Probe on Mem_Write
  // Probe on Next_PC
  // Probe on r08
  // Probe on r09
  // Probe on r10
  // Probe on r11
  // Probe on r12
  // Probe on r13
  // Probe on r14
  // Probe on r15
  Comparator #(.width(4), .mode("unsigned")) comparator_1 (
    .a(Instruction[31:28]), .b(4'b1100), .lt(comparator_1_lt));  // open: gt, eq
  Comparator #(.width(4), .mode("unsigned")) comparator_2 (
    .a(Instruction[31:28]), .b(4'b1101), .gt(comparator_2_gt));  // open: eq, lt
  not not_1 (not_1_out, or_1_out);
  or or_1 (or_1_out, comparator_1_lt, comparator_2_gt);
  assign A_Type = comparator_1_lt ? 2'b10 : 2'bz;  // Controlled_Buffer controlled_buffer_1
  assign A_Type = not_1_out ? 2'b01 : 2'bz;  // Controlled_Buffer controlled_buffer_2
  assign A_Type = comparator_2_gt ? 2'b00 : 2'bz;  // Controlled_Buffer controlled_buffer_3
  Comparator #(.width(4), .mode("unsigned")) comparator_3 (
    .a(Instruction[31:28]), .b(4'b1111), .eq(comparator_3_eq));  // open: gt, lt
  and and_1 (Jump_Cmd, comparator_3_eq, CQ_Output);
  Comparator #(.width(4), .mode("unsigned")) comparator_4 (
    .a(Instruction[31:28]), .b(4'b1010), .eq(comparator_4_eq));  // open: gt, lt
  and and_2 (Load_Cmd, comparator_4_eq, CQ_Output);
  Comparator #(.width(4), .mode("unsigned")) comparator_5 (
    .a(Instruction[31:28]), .b(4'b1011), .eq(comparator_5_eq));  // open: gt, lt
  and and_3 (Mem_Write, comparator_5_eq, CQ_Output);
  assign bit_extender_1_out = {{8{1'b0}}, Instruction[23:8]};  // Bit_Extender bit_extender_1
  assign bit_extender_2_out = {{4{1'b0}}, Instruction[19:0]};  // Bit_Extender bit_extender_2
  Multiplexer #(.select(2), .width(24), .enable("false")) multiplexer_1 (
    .in0(bit_extender_1_out), .in1(bit_extender_2_out), .in2(Instruction[23:0]), .out(out_28), .sel(A_Type));  // open: in3
  assign controlled_buffer_4_out = will_write_to_reg ? Clock : 1'bz;  // Controlled_Buffer controlled_buffer_4
  Comparator #(.width(4), .mode("unsigned")) comparator_6 (
    .a(Instruction[31:28]), .b(4'b1011), .lt(will_write_to_reg));  // open: gt, eq
  Comparator #(.width(2)) comparator_7 (.a(2'b01), .b(A_Type), .eq(comparator_7_eq));  // open: gt, lt
  and and_4 (write, CQ_Output, controlled_buffer_4_out);
  and and_5 (CQ_Cmd, comparator_7_eq, CQ_Output);
  Ida_Register_File ida_register_file_1 (
    .Read_Reg_1(Instruction[3:0]), .Read_Reg_2(Instruction[19:16]), .Write_Reg(Instruction[23:20]),
    .Write_Value(out_32), .Reg_1_Value(out_24), .Reg_2_Value(RS_Result), .Reg_Write(write), .Clock(Clock),
    .r00(r00), .r01(r01), .r02(r02), .r03(r03), .r04(r04), .r05(r05), .r06(r06), .r07(r07), .r08(r08),
    .r09(r09), .r10(r10), .r11(r11), .r12(r12), .r13(r13), .r14(r14), .r15(r15), .Reg_3_Value(RD_Result));
  RAM #(.addrWidth(24), .dataWidth(24), .bus("separate")) ram_1 (
    .addr(out_26), .din(RD_Result), .data(out_32), .str(Mem_Write), .ld(Load_Cmd));  // open: sel, clk, clr
  assign controlled_buffer_5_out = CQ_Cmd ? Clock : 1'bz;  // Controlled_Buffer controlled_buffer_5
  Register #(.width(24)) CQ_Register (
    .D(out_26), .Q({CQ_Register_q, tunnel_t_t, tunnel_t, tunnel}), .clk(controlled_buffer_5_out));  // open: en, clr
  Comparator #(.width(2)) comparator_8 (.a(A_Type), .b(2'b01), .eq(comparator_8_eq));  // open: gt, lt
  Multiplexer #(.width(24), .enable("false")) multiplexer_2 (
    .in0(out_24), .in1(out_28), .out(out_30), .sel(Instruction[24]));
  Multiplexer #(.width(24), .enable("false")) multiplexer_3 (
    .in0(RS_Result), .in1(RD_Result), .out(out_25), .sel(comparator_8_eq));
  or or_2 (or_2_out, tunnel_t, tunnel);
  or or_3 (or_3_out, tunnel_t, tunnel_t_t);
  not not_2 (not_2_out, tunnel_t);
  Multiplexer #(.select(3), .enable("false")) multiplexer_4 (
    .in0(1'b0), .in1(or_2_out), .in2(tunnel_t_t), .in3(not_2_out), .in4(tunnel_t), .in5(or_3_out),
    .in6(tunnel), .in7(1'b1), .out(CQ_Output), .sel(Instruction[27:25]));
  Ida_ALU ida_alu_1 (.ALU_Source_1(out_25), .ALU_Source_2(out_30), .Operation(Instruction[31:28]), .ALU_Result(out_26));
  assign out_32 = will_write_to_reg ? out_26 : 24'bz;  // Controlled_Buffer controlled_buffer_6
  assign bit_extender_3_out = {{23{1'b0}}, 1'b1};  // Bit_Extender bit_extender_3
  Adder #(.width(24)) adder_1 (.a(bit_extender_3_out), .b(Next_PC), .out(adder_1_out));  // open: cin, cout
  Multiplexer #(.width(24), .enable("false")) multiplexer_5 (
    .in0(out_24), .in1(adder_1_out), .out(multiplexer_5_out), .sel(Jump_Cmd));
  assign Mem_Address = or_4_out ? out_26 : 24'bz;  // Controlled_Buffer controlled_buffer_7
  or or_4 (or_4_out, Mem_Write, Load_Cmd);
  assign Mem_Data = Mem_Write ? RD_Result : 24'bz;  // Controlled_Buffer controlled_buffer_8
  Register #(.width(24)) pc (.D(multiplexer_5_out), .Q(Next_PC), .clk(Clock));  // open: en, clr

  assign out_23 = Instruction[31:28];
  assign out_27 = out_25;
  assign out_29 = Instruction[31:28];
  assign out_31 = out_30;
  assign out_33 = out_32;
  assign out_34 = out_26;
  assign out_35 = out_28;

  // Other names for the same wires on the sheet: ALU_Input_1[23:0] = out_25; ALU_Input_2[23:0] = out_30;
  //   ALU_Result[23:0] = out_26; clk = Clock; Direct_Immediate_Value[23:0] = out_28; inst[31:0] = Instruction;
  //   RI_Select[3:0] = Instruction[3:0]; RS_Select[3:0] = Instruction[19:16]; RD_Select[3:0] = Instruction[23:20];
  //   Immediate = Instruction[24]; CQ[2:0] = Instruction[27:25]; OP_Code[3:0] = Instruction[31:28];
  //   memAddr[23:0] = Mem_Address; memData[23:0] = Mem_Data; memWrite = Mem_Write; Save_Cmd = Mem_Write;
  //   nextPC[23:0] = Next_PC; RI_Result[23:0] = out_24; Write_Val[23:0] = out_32

  // Notes on the sheet:
  //   INPUTS
  //   INPUT PROBES
  //   OUTPUT PROBES
  //   OUTPUTS
  //   DO NOT MOVE/ADD/CHANGE ANY INPUT OR OUTPUT PINS!
  //   A-Type Selector
  //   Input Interpretation
  //   Control
  //   CM Stuff
  //   Gather Inputs
  //   Create Value
  //   Result
endmodule
