// Logisim project CPU.circ as structural Verilog: 1 circuit, main circuit Ida CPU
// CPU
module Ida_CPU (
  input  [31:0] Instruction,
  input  Clock,
  output [23:0] Mem_Data,
  output [23:0] Mem_Address,
  output Mem_Write,
  output [23:0] Next_PC,
  output [23:0] r00,
  output [23:0] r01,
  output [23:0] r02,
  output [23:0] r03,
  output [23:0] r04,
  output [23:0] r05,
  output [23:0] r06,
  output [23:0] r07,
  output [23:0] r08,
  output [23:0] r09,
  output [23:0] r10,
  output [23:0] r11,
  output [23:0] r12,
  output [23:0] r13,
  output [23:0] r14,
  output [23:0] r15
);

  // Probe on Instruction
  // Probe on Clock
  // Probe on r00
  // Probe on r01
  // Probe on r02
  // Probe on r03
  // Probe on r04
  // Probe on r05
  // Probe on r06
  // Probe on r07
  // Probe on Mem_Data
  // Probe on Mem_Address
  // Probe on Mem_Write
  // Probe on Next_PC
  // Probe on r08
  // Probe on r09
  // Probe on r10
  // Probe on r11
  // Probe on r12
  // Probe on r13
  // Probe on r14
  // Probe on r15
  Ida_Register_File ida_register_file_1 (
    .r00(r00), .r01(r01), .r02(r02), .r03(r03), .r04(r04), .r05(r05), .r06(r06), .r07(r07), .r08(r08),
    .r09(r09), .r10(r10), .r11(r11), .r12(r12), .r13(r13), .r14(r14), .r15(r15));  // open: Read_Reg_1, Read_Reg_2, Write_Reg, Write_Value, Reg_1_Value, Reg_2_Value, Reg_Write, Clock, Reg_3_Value
  // Ida_ALU ida_alu_1: pin names not known
  RAM #(.addrWidth(24), .dataWidth(24), .bus("separate")) ram_1 ();  // open: addr, din, data, str, sel, clk, ld, clr

  // Other names for the same wires on the sheet: clk = Clock; inst[31:0] = Instruction; memAddr[23:0] = Mem_Address;
  //   memData[23:0] = Mem_Data; memWrite = Mem_Write; nextPC[23:0] = Next_PC

  // Notes on the sheet:
  //   INPUTS
  //   INPUT PROBES
  //   OUTPUT PROBES
  //   OUTPUTS
  //   DO NOT MOVE/ADD/CHANGE ANY INPUT OR OUTPUT PINS!
endmodule
